# Fritzing sketch Connections (saved by Fritzing 1.0.3b)
breadboards: 1

parts:
  Part1 = Arduino Mega 2560 (Rev3)
  Raspberry_Pi_2 = Raspberry Pi 3 [part_number=RPI-3-V1.2]  # not connected
  USBTTL1 = USB A Plug
  USBTTL2 = USB A Plug
  MAX30102_Sensor1 = AS608光学指纹识别模块 [part_number=MAX30102]
  M1 = MPS20N0040D
  M2 = MakerFocus MAX30102
  Mod1 = gy-906

nets:
  N1: Part1.D21/SCL, M2.SCL, Mod1.SCL
  N2: Part1.D20/SDA, M2.SDA, Mod1.SDA
  N3: Part1.D18/TX1, MAX30102_Sensor1.pin_5
  GND: Part1.GND, MAX30102_Sensor1.pin_4, M1.GND, M2.GND, Mod1.GND
  N4: Part1.3V3, MAX30102_Sensor1.pin_1, MAX30102_Sensor1.pin_6
  N5: Part1.D0_RX0, MAX30102_Sensor1.pin_2
  N6: Part1.D1_TX0, MAX30102_Sensor1.pin_3
  N7: Part1.D2_PWM, M1.OUT
  N8: Part1.D3_PWM, M1.SCK
  VIN: Part1.5V, M1.VCC, M2.VIN, Mod1.VIN
  N9: USBTTL1.usb, USBTTL2.usb
  N10: MAX30102_Sensor1.pin_7, MAX30102_Sensor1.pin_8

custom parts:
  AS608光学指纹识别模块: The MAX30102 is an integrated pulse oximetry and heart-rate monitor biosensor module. It includes internal LEDs, photodetectors, optical elements, and low-noise electronics with ambient light rejection. The MAX30102 operates on a single 1.8V power supply and a separate 3.3V power supply for the internal LEDs. Communication is through a I2C-compatible interface.
  MPS20N0040D: MPS20N0040D Sphygmomanometer 0-40kPa Differential Air Pressure Sensor / HX710B ADC Module This module couples a MPS20N0040D sphygmomanometer air pressure sensor module with an HX710B analog-to-digital converter IC. It can be powered from a 3.3V or 5V source, with a claimed measurement range of 0-40kPa. It uses a proprietary 2-wire communication protocol and is thus not I2C compatible. Links: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
  MakerFocus MAX30102: Oximeter module using the MAX30102 chip. As usual, if you want the mounting holes in pcb, you need to drag a hole over the pad in silkscreen to actually drill the hole (by default they are not drilled)
  gy-906: gy-906 Non-contact PIR I2C interface temperature sensor breakout board.
