# Fritzing sketch PARTS OF ROBOط (saved by Fritzing 1.0.3b)

parts:
  Part1 = Arduino Mega 2560 (Rev3)
  U1 = TRANSCHIPTC5747 [package=camera_sfv24r-2st_2]  # not connected
  Raspberry_Pi_1 = Raspberry Pi 3 [part_number=RPI-3-V1.2]  # not connected
  BAT1 = 12 battery [package=battery]  # not connected
  SPKR1 = Loudspeaker  # not connected
  Part2 = Arduino Color LCD Shield  # not connected
  Part3 = sensor_biometrico
  M1 = MakerFocus MAX30102
  Mod1 = gy-906

nets:
  N1: Part1.D21/SCL, M1.SCL, Mod1.SCL
  N2: Part1.D20/SDA, M1.SDA, Mod1.SDA
  GND: Part1.GND, Part3.GND, M1.GND, Mod1.GND
  5V: Part1.5V, Part3.VCC, Mod1.VIN
  N3: Part1.D0_RX0, Part3.RX
  N4: Part1.D1_TX0, Part3.TX

custom parts:
  12 battery: 12V lead acid type battery, like the Husqvarna YTH2448 12V 35AH battery. This is the mini version 1/4 the size of the actual battery to be closer to typical breadboard parts (around 2in wide rathher than 7in). The pads in pcb are sized to accomidate up to 14ga wire (as these batterys will deliver high currents.)
  sensor_biometrico: Adafruit Optical Fingerprint Sensor
  MakerFocus MAX30102: Oximeter module using the MAX30102 chip. As usual, if you want the mounting holes in pcb, you need to drag a hole over the pad in silkscreen to actually drill the hole (by default they are not drilled)
  gy-906: gy-906 Non-contact PIR I2C interface temperature sensor breakout board.
